# Fritzing sketch emoncore v1 (saved by Fritzing 0.9.2b)
circuit board: 5cm x 8.9cm

parts:
  U3 = 3.5mm Audio Jack [package=audio-jack-3.5mm-smd]
  R1 = Resistor [tolerance=±5% resistance=22k package=THT]
  R2 = Resistor [tolerance=±5% resistance=22k package=THT]
  C1 = Electrolytic Capacitor [capacitance=1µF voltage=10V package="100 mil [THT, electrolytic]"]
  R3 = Resistor [tolerance=±5% resistance=22 package=THT]
  U4 = 3.5mm Audio Jack [package=audio-jack-3.5mm-smd]
  R4 = Resistor [tolerance=±5% resistance=22 package=THT]
  U5 = 3.5mm Audio Jack [package=audio-jack-3.5mm-smd]
  R5 = Resistor [tolerance=±5% resistance=22 package=THT]
  U6 = 3.5mm Audio Jack [package=audio-jack-3.5mm-smd]
  R6 = Resistor [tolerance=±5% resistance=22 package=THT]
  U7 = 3.5mm Audio Jack [package=audio-jack-3.5mm-smd]
  R7 = Resistor [tolerance=±5% resistance=22 package=THT]
  U8 = 3.5mm Audio Jack [package=audio-jack-3.5mm-smd]
  R8 = Resistor [tolerance=±5% resistance=22 package=THT]
  U9 = 3.5mm Audio Jack [package=audio-jack-3.5mm-smd]
  R9 = Resistor [tolerance=±5% resistance=22 package=THT]
  R10 = Resistor [tolerance=±5% resistance=4.7k package=THT]
  R11 = Resistor [tolerance=±5% resistance=4.7k package=THT]
  LED1 = LED - 5mm [color="Red (633nm)" package="5 mm [THT]"]
  R12 = Resistor [tolerance=±5% resistance=220 package=THT]
  R13 = Resistor [tolerance=±5% resistance=100k package=THT]
  R14 = Resistor [tolerance=±5% resistance=10k package=THT]
  Voltage_Sense = Power plug
  J1 = male pin header, 4 pins [form="♂ (male)"]
  U10 = Spark Core (v1.0)  # not connected
  U2 = LM 358 Dual Op-Amp [package="DIP8 [THT]"]
  J2 = female pin header, 2 pins [form="♀ (female)"]
  J3 = female pin header, 3 pins [form="♀ (female)"]
  J4 = female pin header, 12 pins [form="♀ (female)"]
  J5 = female pin header, 12 pins [form="♀ (female)"]

nets:
  ct1: U3.SLEEVE, R3.Pin_0, J4.pin11
  vMid: U3.LEFT, R3.Pin_1, U4.LEFT, R4.Pin_1, U5.LEFT, R5.Pin_1, U6.LEFT, R6.Pin_1, U7.LEFT, R7.Pin_1, U8.LEFT, R8.Pin_1, U9.LEFT, R9.Pin_1, R14.Pin_0, Voltage_Sense.GND, U2.connector0, U2.connector1, J3.pin3
  N1: R1.Pin_0, J5.pin3
  N2: R1.Pin_1, R2.Pin_1, C1.+, U2.connector2
  GND: R2.Pin_0, C1.-, R12.Pin_1, J1.pin4, U2.connector4, U2.connector7, J2.pin1, J4.pin2, J5.pin4
  ct2: U4.SLEEVE, R4.Pin_0, J4.pin10
  ct3: U5.SLEEVE, R5.Pin_0, J4.pin9
  ct4: U6.SLEEVE, R6.Pin_0, J4.pin8
  ct5: U7.SLEEVE, R7.Pin_0, J4.pin7
  ct6: U8.SLEEVE, R8.Pin_0, J4.pin6
  ct7: U9.SLEEVE, R9.Pin_0, J4.pin5
  N3: R10.Pin_0, J1.pin2, J3.pin2, J5.pin12
  N4: R10.Pin_1, R11.Pin_1, J1.pin3, U2.connector3, J2.pin2, J5.pin1
  N5: R11.Pin_0, J1.pin1, J3.pin1, J5.pin11
  N6: LED1.cathode, R12.Pin_0
  N7: LED1.anode, J5.pin5
  N8: R13.Pin_0, Voltage_Sense.VCC
  volts: R13.Pin_1, R14.Pin_1, J4.pin12
  N9: U2.connector5, U2.connector6

notes:
  Open Energy Monitor Spark Core, All In One Energy Monitor, 0.1
  emoncore

custom parts:
  Spark Core (v1.0): The Spark Core is a tiny Wi-Fi development board that makes it easy to create internet-connected hardware. The Core is all you need to get started; power it over USB and in minutes you'll be controlling LEDs, switches and motors and collecting data from sensors over the internet! It has 8 digital I/O pins, 8 analog I/O pins, 8 PWM pins; UART (Serial), SPI, I2C, and JTAG peripherals available.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
